// Digital circuit ALU.dig as structural Verilog
module ALU (
  input  clk,
  input  clk_2,
  input  [7:0] A0,
  input  [7:0] B0,
  input  Dir,
  input  [1:0] Sel,
  input  [2:0] Sel_2
);

  wire [3:0] AC_q, AC_q_2, MQ_q, MQ_q_2;
  wire [7:0] multiplexer_1_out, multiplexer_2_out, \Multiplicação__LSB , \Multiplicação__MSB , NAND,
       Quociente, Resto, \Shift_Lógico , Soma, \Subtração , XOR;

  somador_8bits somador_8bits_1 (
    .A0(A0[0]), .B0(B0[0]), .A1(A0[1]), .B1(B0[1]), .A2(A0[2]), .B2(B0[2]), .A3(A0[3]), .B3(B0[3]),
    .A4(A0[4]), .B4(B0[4]), .A5(A0[5]), .B5(B0[5]), .A6(A0[6]), .B6(B0[6]), .A7(A0[7]), .B7(B0[7]),
    .Ci(1'b0), .S0(Soma[0]), .S1(Soma[1]), .S2(Soma[2]), .S3(Soma[3]), .S4(Soma[4]), .S5(Soma[5]),
    .S6(Soma[6]), .S7(Soma[7]));  // open: Co
  subtrator_8bits subtrator_8bits_1 (
    .A0(A0[0]), .B0(B0[0]), .A1(A0[1]), .B1(B0[1]), .A2(A0[2]), .B2(B0[2]), .A3(A0[3]), .B3(B0[3]),
    .A4(A0[4]), .B4(B0[4]), .A5(A0[5]), .B5(B0[5]), .A6(A0[6]), .B6(B0[6]), .A7(A0[7]), .B7(B0[7]),
    .S0(\Subtração [0]), .S1(\Subtração [1]), .S2(\Subtração [2]), .S3(\Subtração [3]), .S4(\Subtração [4]),
    .S5(\Subtração [5]), .S6(\Subtração [6]), .S7(\Subtração [7]));  // open: Co
  multiplicador_8bits multiplicador_8bits_1 (
    .A0(A0[0]), .A1(A0[1]), .A2(A0[2]), .A3(A0[3]), .A4(A0[4]), .A5(A0[5]), .A6(A0[6]), .A7(A0[7]),
    .B0(B0[0]), .B1(B0[1]), .B2(B0[2]), .B3(B0[3]), .B4(B0[4]), .B5(B0[5]), .B6(B0[6]), .B7(B0[7]),
    .S0(\Multiplicação__LSB [0]), .S1(\Multiplicação__LSB [1]), .S2(\Multiplicação__LSB [2]),
    .S3(\Multiplicação__LSB [3]), .S4(\Multiplicação__LSB [4]), .S5(\Multiplicação__LSB [5]),
    .S6(\Multiplicação__LSB [6]), .S7(\Multiplicação__LSB [7]), .S8(\Multiplicação__MSB [0]),
    .S9(\Multiplicação__MSB [1]), .S10(\Multiplicação__MSB [2]), .S11(\Multiplicação__MSB [3]),
    .S12(\Multiplicação__MSB [4]), .S13(\Multiplicação__MSB [5]), .S14(\Multiplicação__MSB [6]),
    .S15(\Multiplicação__MSB [7]));
  divisor_de_8bits divisor_de_8bits_1 (
    .D0(A0[0]), .D1(A0[1]), .D2(A0[2]), .D3(A0[3]), .D4(A0[4]), .D5(A0[5]), .D6(A0[6]), .D7(A0[7]),
    .d0_2(B0[0]), .d1_2(B0[1]), .d2_2(B0[2]), .d3_2(B0[3]), .d4_2(B0[4]), .d5_2(B0[5]), .d6_2(B0[6]),
    .d7_2(B0[7]), .Q7(Quociente[7]), .Q6(Quociente[6]), .Q5(Quociente[5]), .Q4(Quociente[4]),
    .Q3(Quociente[3]), .Q2(Quociente[2]), .Q1(Quociente[1]), .Q0(Quociente[0]), .r0(Resto[0]), .r1(Resto[1]),
    .r2(Resto[2]), .r3(Resto[3]), .r4(Resto[4]), .r5(Resto[5]), .r6(Resto[6]), .r7(Resto[7]));
  \shift_lógico  \shift_lógico_1  (
    .B0(B0[0]), .B1(B0[1]), .B2(B0[2]), .B3(B0[3]), .B4(B0[4]), .B5(B0[5]), .B6(B0[6]), .B7(B0[7]),
    .Dir(Dir), .S0(\Shift_Lógico [0]), .S1(\Shift_Lógico [1]), .S2(\Shift_Lógico [2]),
    .S3(\Shift_Lógico [3]), .S4(\Shift_Lógico [4]), .S5(\Shift_Lógico [5]), .S6(\Shift_Lógico [6]),
    .S7(\Shift_Lógico [7]));
  NAND nand_1 (.A(A0), .B(B0), .S(NAND));
  XOR xor_1 (.A(A0), .B(B0), .S(XOR));
  D_FF #(.Bits(8)) MQ (.D(multiplexer_1_out), .C(clk_2), .Q({MQ_q_2, MQ_q}));  // open: nQ
  Multiplexer #(.Selector_Bits(2), .Bits(8)) multiplexer_1 (
    .sel(Sel), .in_0({8{1'b0}}), .in_1(\Multiplicação__MSB ), .in_2(Quociente), .in_3({8{1'b0}}),
    .out(multiplexer_1_out));
  Seven_Seg_Hex seven_seg_hex_1 (.d(MQ_q_2), .dp(1'b0));
  Seven_Seg_Hex seven_seg_hex_2 (.d(MQ_q), .dp(1'b0));
  Seven_Seg_Hex seven_seg_hex_3 (.d(AC_q_2), .dp(1'b0));
  D_FF #(.Bits(8)) AC (.D(multiplexer_2_out), .C(clk), .Q({AC_q_2, AC_q}));  // open: nQ
  Seven_Seg_Hex seven_seg_hex_4 (.d(AC_q), .dp(1'b0));
  Multiplexer #(.Selector_Bits(3), .Bits(8)) multiplexer_2 (
    .sel(Sel_2), .in_0(Soma), .in_1(\Subtração ), .in_2(\Multiplicação__LSB ), .in_3(Resto),
    .in_4(\Shift_Lógico ), .in_5(NAND), .in_6(XOR), .in_7({8{1'b0}}), .out(multiplexer_2_out));

  // Other names for the same wires on the sheet: A[7:0] = A0; A0_t = A0[0]; A1 = A0[1]; A2 = A0[2]; A3 = A0[3];
  //   A4 = A0[4]; A5 = A0[5]; A6 = A0[6]; A7 = A0[7]; B[7:0] = B0; B0_t = B0[0]; B1 = B0[1]; B2 = B0[2]; B3 = B0[3];
  //   B4 = B0[4]; B5 = B0[5]; B6 = B0[6]; B7 = B0[7]
endmodule
