// Digital circuit XOR 1bit.dig as structural Verilog
module XOR_1bit (
  input  A0,
  input  B0,
  output S0
);

  wire and_1_out, not_1_out, or_1_out;

  or or_1 (or_1_out, A0, B0);
  and and_1 (and_1_out, A0, B0);
  not not_1 (not_1_out, and_1_out);
  and and_2 (S0, or_1_out, not_1_out);
endmodule
