// Digital circuit divisor de 8bits.dig as structural Verilog
module divisor_de_8bits (
  input  D0,
  input  D1,
  input  D2,
  input  D3,
  input  D4,
  input  D5,
  input  D6,
  input  D7,
  input  d0_2,
  input  d1_2,
  input  d2_2,
  input  d3_2,
  input  d4_2,
  input  d5_2,
  input  d6_2,
  input  d7_2,
  output Q7,
  output Q6,
  output Q5,
  output Q4,
  output Q3,
  output Q2,
  output Q1,
  output Q0,
  output r0,
  output r1,
  output r2,
  output r3,
  output r4,
  output r5,
  output r6,
  output r7
);

  wire d0_t, d1_t, d2_t, d3_t, d4_t, d5_t, d6_t, d7_t, M0, M1, M2, M3, M4, M5, M6, M7, M8, M9, M10, M11, M12,
       M13, M14, M15, M16, M17, M18, M19, M20, M21, M22, M23, M24, M25, M26, M27, M28, M29, M30, M31, M32,
       M33, M34, M35, M36, M37, M38, M39, M40, M41, M42, M43, M44, M45, M46, M47, M48, M49, M50, M51, M52,
       M53, M54, M55, not_1_out, not_2_out, not_4_out, not_6_out, not_8_out, not_10_out, not_12_out, S0, S1,
       S2, S3, S4, S5, S6, S7, S8, S9, S10, S11, S12, S13, S14, S15, S16, S17, S18, S19, S20, S21, S22, S23,
       S24, S25, S26, S27, S28, S29, S30, S31, S32, S33, S34, S35, S36, S37, S38, S39, S40, S41, S42, S43,
       S44, S45, S46, S47, S48, S49, S50, S51, S52, S53, S54, S55, S56, S57, S58, S59, S60, S61, S62, S63,
       soma_3_co, soma_4_co, soma_6_co, soma_7_co, soma_8_co, soma_10_co, soma_11_co, soma_12_co, soma_13_co,
       soma_15_co, soma_16_co, soma_17_co, soma_18_co, soma_19_co, soma_21_co, soma_22_co, soma_23_co,
       soma_24_co, soma_25_co, soma_26_co, soma_28_co, soma_29_co, soma_30_co, soma_31_co, soma_32_co,
       soma_33_co, soma_34_co, soma_36_co, soma_37_co, soma_38_co, soma_39_co, soma_40_co, soma_41_co,
       soma_42_co, soma_43_co, soma_44_co, soma_45_co, soma_46_co, soma_47_co, soma_48_co, soma_49_co,
       soma_50_co, soma_51_co, soma_52_co, soma_53_co, soma_54_co, soma_55_co, soma_56_co, soma_57_co,
       soma_58_co, soma_59_co, soma_60_co, soma_61_co, soma_62_co, soma_63_co, soma_64_co, soma_65_co,
       soma_66_co, soma_67_co, soma_68_co, soma_69_co, soma_70_co, soma_71_co;

  not not_1 (not_1_out, 1'b0);
  soma soma_1 (.A(1'b0), .B(d7_t), .Ci(soma_3_co), .Co(Q7), .S(S57));
  Multiplexer multiplexer_1 (.sel(Q7), .in_0(1'b0), .in_1(S57), .out(M49));
  soma soma_2 (.A(M49), .B(not_1_out), .Ci(soma_4_co), .Co(Q6));  // open: S
  not not_2 (not_2_out, 1'b0);
  not not_3 (d7_t, d7_2);
  soma soma_3 (.A(1'b0), .B(d6_t), .Ci(soma_6_co), .Co(soma_3_co), .S(S6));
  Multiplexer multiplexer_2 (.sel(Q7), .in_0(1'b0), .in_1(S6), .out(M6));
  soma soma_4 (.A(M6), .B(d7_t), .Ci(soma_7_co), .Co(soma_4_co), .S(S58));
  Multiplexer multiplexer_3 (.sel(Q6), .in_0(M6), .in_1(S58), .out(M50));
  soma soma_5 (.A(M50), .B(not_2_out), .Ci(soma_8_co), .Co(Q5));  // open: S
  not not_4 (not_4_out, 1'b0);
  not not_5 (d6_t, d6_2);
  soma soma_6 (.A(1'b0), .B(d5_t), .Ci(soma_10_co), .Co(soma_6_co), .S(S5));
  Multiplexer multiplexer_4 (.sel(Q7), .in_0(1'b0), .in_1(S5), .out(M5));
  soma soma_7 (.A(M5), .B(d6_t), .Ci(soma_11_co), .Co(soma_7_co), .S(S13));
  Multiplexer multiplexer_5 (.sel(Q6), .in_0(M5), .in_1(S13), .out(M13));
  soma soma_8 (.A(M13), .B(d7_t), .Ci(soma_12_co), .Co(soma_8_co), .S(S59));
  Multiplexer multiplexer_6 (.sel(Q5), .in_0(M13), .in_1(S59), .out(M51));
  soma soma_9 (.A(M51), .B(not_4_out), .Ci(soma_13_co), .Co(Q4));  // open: S
  not not_6 (not_6_out, 1'b0);
  not not_7 (d5_t, d5_2);
  soma soma_10 (.A(1'b0), .B(d4_t), .Ci(soma_15_co), .Co(soma_10_co), .S(S4));
  Multiplexer multiplexer_7 (.sel(Q7), .in_0(1'b0), .in_1(S4), .out(M4));
  soma soma_11 (.A(M4), .B(d5_t), .Ci(soma_16_co), .Co(soma_11_co), .S(S12));
  Multiplexer multiplexer_8 (.sel(Q6), .in_0(M4), .in_1(S12), .out(M12));
  soma soma_12 (.A(M12), .B(d6_t), .Ci(soma_17_co), .Co(soma_12_co), .S(S20));
  Multiplexer multiplexer_9 (.sel(Q5), .in_0(M12), .in_1(S20), .out(M20));
  soma soma_13 (.A(M20), .B(d7_t), .Ci(soma_18_co), .Co(soma_13_co), .S(S60));
  Multiplexer multiplexer_10 (.sel(Q4), .in_0(M20), .in_1(S60), .out(M52));
  soma soma_14 (.A(M52), .B(not_6_out), .Ci(soma_19_co), .Co(Q3));  // open: S
  not not_8 (not_8_out, 1'b0);
  not not_9 (d4_t, d4_2);
  soma soma_15 (.A(1'b0), .B(d3_t), .Ci(soma_21_co), .Co(soma_15_co), .S(S3));
  Multiplexer multiplexer_11 (.sel(Q7), .in_0(1'b0), .in_1(S3), .out(M3));
  soma soma_16 (.A(M3), .B(d4_t), .Ci(soma_22_co), .Co(soma_16_co), .S(S11));
  Multiplexer multiplexer_12 (.sel(Q6), .in_0(M3), .in_1(S11), .out(M11));
  soma soma_17 (.A(M11), .B(d5_t), .Ci(soma_23_co), .Co(soma_17_co), .S(S19));
  Multiplexer multiplexer_13 (.sel(Q5), .in_0(M11), .in_1(S19), .out(M19));
  soma soma_18 (.A(M19), .B(d6_t), .Ci(soma_24_co), .Co(soma_18_co), .S(S27));
  Multiplexer multiplexer_14 (.sel(Q4), .in_0(M19), .in_1(S27), .out(M27));
  soma soma_19 (.A(M27), .B(d7_t), .Ci(soma_25_co), .Co(soma_19_co), .S(S61));
  Multiplexer multiplexer_15 (.sel(Q3), .in_0(M27), .in_1(S61), .out(M53));
  soma soma_20 (.A(M53), .B(not_8_out), .Ci(soma_26_co), .Co(Q2));  // open: S
  not not_10 (not_10_out, 1'b0);
  not not_11 (d3_t, d3_2);
  soma soma_21 (.A(1'b0), .B(d2_t), .Ci(soma_28_co), .Co(soma_21_co), .S(S2));
  Multiplexer multiplexer_16 (.sel(Q7), .in_0(1'b0), .in_1(S2), .out(M2));
  soma soma_22 (.A(M2), .B(d3_t), .Ci(soma_29_co), .Co(soma_22_co), .S(S10));
  Multiplexer multiplexer_17 (.sel(Q6), .in_0(M2), .in_1(S10), .out(M10));
  soma soma_23 (.A(M10), .B(d4_t), .Ci(soma_30_co), .Co(soma_23_co), .S(S18));
  Multiplexer multiplexer_18 (.sel(Q5), .in_0(M10), .in_1(S18), .out(M18));
  soma soma_24 (.A(M18), .B(d5_t), .Ci(soma_31_co), .Co(soma_24_co), .S(S26));
  Multiplexer multiplexer_19 (.sel(Q4), .in_0(M18), .in_1(S26), .out(M26));
  soma soma_25 (.A(M26), .B(d6_t), .Ci(soma_32_co), .Co(soma_25_co), .S(S34));
  Multiplexer multiplexer_20 (.sel(Q3), .in_0(M26), .in_1(S34), .out(M34));
  soma soma_26 (.A(M34), .B(d7_t), .Ci(soma_33_co), .Co(soma_26_co), .S(S62));
  Multiplexer multiplexer_21 (.sel(Q2), .in_0(M34), .in_1(S62), .out(M54));
  soma soma_27 (.A(M54), .B(not_10_out), .Ci(soma_34_co), .Co(Q1));  // open: S
  not not_12 (not_12_out, 1'b0);
  not not_13 (d2_t, d2_2);
  soma soma_28 (.A(1'b0), .B(d1_t), .Ci(soma_36_co), .Co(soma_28_co), .S(S1));
  Multiplexer multiplexer_22 (.sel(Q7), .in_0(1'b0), .in_1(S1), .out(M1));
  soma soma_29 (.A(M1), .B(d2_t), .Ci(soma_37_co), .Co(soma_29_co), .S(S9));
  Multiplexer multiplexer_23 (.sel(Q6), .in_0(M1), .in_1(S9), .out(M9));
  soma soma_30 (.A(M9), .B(d3_t), .Ci(soma_38_co), .Co(soma_30_co), .S(S17));
  Multiplexer multiplexer_24 (.sel(Q5), .in_0(M9), .in_1(S17), .out(M17));
  soma soma_31 (.A(M17), .B(d4_t), .Ci(soma_39_co), .Co(soma_31_co), .S(S25));
  Multiplexer multiplexer_25 (.sel(Q4), .in_0(M17), .in_1(S25), .out(M25));
  soma soma_32 (.A(M25), .B(d5_t), .Ci(soma_40_co), .Co(soma_32_co), .S(S33));
  Multiplexer multiplexer_26 (.sel(Q3), .in_0(M25), .in_1(S33), .out(M33));
  soma soma_33 (.A(M33), .B(d6_t), .Ci(soma_41_co), .Co(soma_33_co), .S(S41));
  Multiplexer multiplexer_27 (.sel(Q2), .in_0(M33), .in_1(S41), .out(M41));
  soma soma_34 (.A(M41), .B(d7_t), .Ci(soma_42_co), .Co(soma_34_co), .S(S63));
  Multiplexer multiplexer_28 (.sel(Q1), .in_0(M41), .in_1(S63), .out(M55));
  soma soma_35 (.A(M55), .B(not_12_out), .Ci(soma_43_co), .Co(Q0));  // open: S
  not not_14 (d1_t, d1_2);
  soma soma_36 (.A(D7), .B(d0_t), .Ci(1'b1), .Co(soma_36_co), .S(S0));
  Multiplexer multiplexer_29 (.sel(Q7), .in_0(D7), .in_1(S0), .out(M0));
  soma soma_37 (.A(M0), .B(d1_t), .Ci(soma_44_co), .Co(soma_37_co), .S(S8));
  Multiplexer multiplexer_30 (.sel(Q6), .in_0(M0), .in_1(S8), .out(M8));
  soma soma_38 (.A(M8), .B(d2_t), .Ci(soma_45_co), .Co(soma_38_co), .S(S16));
  Multiplexer multiplexer_31 (.sel(Q5), .in_0(M8), .in_1(S16), .out(M16));
  soma soma_39 (.A(M16), .B(d3_t), .Ci(soma_46_co), .Co(soma_39_co), .S(S24));
  Multiplexer multiplexer_32 (.sel(Q4), .in_0(M16), .in_1(S24), .out(M24));
  soma soma_40 (.A(M24), .B(d4_t), .Ci(soma_47_co), .Co(soma_40_co), .S(S32));
  Multiplexer multiplexer_33 (.sel(Q3), .in_0(M24), .in_1(S32), .out(M32));
  soma soma_41 (.A(M32), .B(d5_t), .Ci(soma_48_co), .Co(soma_41_co), .S(S40));
  Multiplexer multiplexer_34 (.sel(Q2), .in_0(M32), .in_1(S40), .out(M40));
  soma soma_42 (.A(M40), .B(d6_t), .Ci(soma_49_co), .Co(soma_42_co), .S(S48));
  Multiplexer multiplexer_35 (.sel(Q1), .in_0(M40), .in_1(S48), .out(M48));
  soma soma_43 (.A(M48), .B(d7_t), .Ci(soma_50_co), .Co(soma_43_co), .S(S56));
  Multiplexer multiplexer_36 (.sel(Q0), .in_0(M48), .in_1(S56), .out(r7));
  not not_15 (d0_t, d0_2);
  soma soma_44 (.A(D6), .B(d0_t), .Ci(1'b1), .Co(soma_44_co), .S(S7));
  Multiplexer multiplexer_37 (.sel(Q6), .in_0(D6), .in_1(S7), .out(M7));
  soma soma_45 (.A(M7), .B(d1_t), .Ci(soma_51_co), .Co(soma_45_co), .S(S15));
  Multiplexer multiplexer_38 (.sel(Q5), .in_0(M7), .in_1(S15), .out(M15));
  soma soma_46 (.A(M15), .B(d2_t), .Ci(soma_52_co), .Co(soma_46_co), .S(S23));
  Multiplexer multiplexer_39 (.sel(Q4), .in_0(M15), .in_1(S23), .out(M23));
  soma soma_47 (.A(M23), .B(d3_t), .Ci(soma_53_co), .Co(soma_47_co), .S(S31));
  Multiplexer multiplexer_40 (.sel(Q3), .in_0(M23), .in_1(S31), .out(M31));
  soma soma_48 (.A(M31), .B(d4_t), .Ci(soma_54_co), .Co(soma_48_co), .S(S39));
  Multiplexer multiplexer_41 (.sel(Q2), .in_0(M31), .in_1(S39), .out(M39));
  soma soma_49 (.A(M39), .B(d5_t), .Ci(soma_55_co), .Co(soma_49_co), .S(S47));
  Multiplexer multiplexer_42 (.sel(Q1), .in_0(M39), .in_1(S47), .out(M47));
  soma soma_50 (.A(M47), .B(d6_t), .Ci(soma_56_co), .Co(soma_50_co), .S(S55));
  Multiplexer multiplexer_43 (.sel(Q0), .in_0(M47), .in_1(S55), .out(r6));
  soma soma_51 (.A(D5), .B(d0_t), .Ci(1'b1), .Co(soma_51_co), .S(S14));
  Multiplexer multiplexer_44 (.sel(Q5), .in_0(D5), .in_1(S14), .out(M14));
  soma soma_52 (.A(M14), .B(d1_t), .Ci(soma_57_co), .Co(soma_52_co), .S(S22));
  Multiplexer multiplexer_45 (.sel(Q4), .in_0(M14), .in_1(S22), .out(M22));
  soma soma_53 (.A(M22), .B(d2_t), .Ci(soma_58_co), .Co(soma_53_co), .S(S30));
  Multiplexer multiplexer_46 (.sel(Q3), .in_0(M22), .in_1(S30), .out(M30));
  soma soma_54 (.A(M30), .B(d3_t), .Ci(soma_59_co), .Co(soma_54_co), .S(S38));
  Multiplexer multiplexer_47 (.sel(Q2), .in_0(M30), .in_1(S38), .out(M38));
  soma soma_55 (.A(M38), .B(d4_t), .Ci(soma_60_co), .Co(soma_55_co), .S(S46));
  Multiplexer multiplexer_48 (.sel(Q1), .in_0(M38), .in_1(S46), .out(M46));
  soma soma_56 (.A(M46), .B(d5_t), .Ci(soma_61_co), .Co(soma_56_co), .S(S54));
  Multiplexer multiplexer_49 (.sel(Q0), .in_0(M46), .in_1(S54), .out(r5));
  soma soma_57 (.A(D4), .B(d0_t), .Ci(1'b1), .Co(soma_57_co), .S(S21));
  Multiplexer multiplexer_50 (.sel(Q4), .in_0(D4), .in_1(S21), .out(M21));
  soma soma_58 (.A(M21), .B(d1_t), .Ci(soma_62_co), .Co(soma_58_co), .S(S29));
  Multiplexer multiplexer_51 (.sel(Q3), .in_0(M21), .in_1(S29), .out(M29));
  soma soma_59 (.A(M29), .B(d2_t), .Ci(soma_63_co), .Co(soma_59_co), .S(S37));
  Multiplexer multiplexer_52 (.sel(Q2), .in_0(M29), .in_1(S37), .out(M37));
  soma soma_60 (.A(M37), .B(d3_t), .Ci(soma_64_co), .Co(soma_60_co), .S(S45));
  Multiplexer multiplexer_53 (.sel(Q1), .in_0(M37), .in_1(S45), .out(M45));
  soma soma_61 (.A(M45), .B(d4_t), .Ci(soma_65_co), .Co(soma_61_co), .S(S53));
  Multiplexer multiplexer_54 (.sel(Q0), .in_0(M45), .in_1(S53), .out(r4));
  soma soma_62 (.A(D3), .B(d0_t), .Ci(1'b1), .Co(soma_62_co), .S(S28));
  Multiplexer multiplexer_55 (.sel(Q3), .in_0(D3), .in_1(S28), .out(M28));
  soma soma_63 (.A(M28), .B(d1_t), .Ci(soma_66_co), .Co(soma_63_co), .S(S36));
  Multiplexer multiplexer_56 (.sel(Q2), .in_0(M28), .in_1(S36), .out(M36));
  soma soma_64 (.A(M36), .B(d2_t), .Ci(soma_67_co), .Co(soma_64_co), .S(S44));
  Multiplexer multiplexer_57 (.sel(Q1), .in_0(M36), .in_1(S44), .out(M44));
  soma soma_65 (.A(M44), .B(d3_t), .Ci(soma_68_co), .Co(soma_65_co), .S(S52));
  Multiplexer multiplexer_58 (.sel(Q0), .in_0(M44), .in_1(S52), .out(r3));
  soma soma_66 (.A(D2), .B(d0_t), .Ci(1'b1), .Co(soma_66_co), .S(S35));
  Multiplexer multiplexer_59 (.sel(Q2), .in_0(D2), .in_1(S35), .out(M35));
  soma soma_67 (.A(M35), .B(d1_t), .Ci(soma_69_co), .Co(soma_67_co), .S(S43));
  Multiplexer multiplexer_60 (.sel(Q1), .in_0(M35), .in_1(S43), .out(M43));
  soma soma_68 (.A(M43), .B(d2_t), .Ci(soma_70_co), .Co(soma_68_co), .S(S51));
  Multiplexer multiplexer_61 (.sel(Q0), .in_0(M43), .in_1(S51), .out(r2));
  soma soma_69 (.A(D1), .B(d0_t), .Ci(1'b1), .Co(soma_69_co), .S(S42));
  Multiplexer multiplexer_62 (.sel(Q1), .in_0(D1), .in_1(S42), .out(M42));
  soma soma_70 (.A(M42), .B(d1_t), .Ci(soma_71_co), .Co(soma_70_co), .S(S50));
  Multiplexer multiplexer_63 (.sel(Q0), .in_0(M42), .in_1(S50), .out(r1));
  soma soma_71 (.A(D0), .B(d0_t), .Ci(1'b1), .Co(soma_71_co), .S(S49));
  Multiplexer multiplexer_64 (.sel(Q0), .in_0(D0), .in_1(S49), .out(r0));
endmodule
