// Digital circuit meio-subtrator.dig as structural Verilog
module meio_subtrator (
  input  A,
  input  B,
  output S,
  output Co
);

  wire not_1_out;

  not not_1 (not_1_out, A);
  xor xor_1 (S, B, A);
  and and_1 (Co, B, not_1_out);
endmodule
