// Digital circuit multiplicador 2bits.dig as structural Verilog
module multiplicador_2bits (
  input  B1,
  input  B0,
  input  A1,
  input  A0,
  output S0,
  output S1,
  output S2,
  output S3
);

  multiplicador multiplicador_1 (.B1(B1), .B0(B0), .A1(A1), .A0(A0), .S3(S3), .S2(S2), .S1(S1), .S0(S0));
endmodule
