// Digital circuit multiplicador 4bits errado.dig as structural Verilog
module multiplicador_4bits_errado (
  input  A0,
  input  A1,
  input  B0,
  input  B1,
  input  A2,
  input  A3,
  input  B2,
  input  B3,
  output S0,
  output S1,
  output S2,
  output S3,
  output S4,
  output S5,
  output S6,
  output S7
);

  wire Ci1, Ci2, Ci3, Ci4, Ci5, multiplicador_2bits_1_s1, multiplicador_2bits_1_s2, multiplicador_2bits_1_s3,
       multiplicador_2bits_2_s0, multiplicador_2bits_2_s1, multiplicador_2bits_2_s2,
       multiplicador_2bits_2_s3, multiplicador_2bits_3_s0, multiplicador_2bits_3_s1,
       multiplicador_2bits_3_s2, multiplicador_2bits_3_s3, multiplicador_2bits_4_s0,
       multiplicador_2bits_4_s1, multiplicador_2bits_4_s2, multiplicador_2bits_4_s3, soma_1_co, soma_1_s,
       soma_2_co, soma_2_s, soma_4_co, soma_4_s, soma_6_co, soma_6_s;

  multiplicador_2bits multiplicador_2bits_1 (
    .B1(B1), .B0(B0), .A1(A1), .A0(A0), .S0(S0), .S1(multiplicador_2bits_1_s1),
    .S2(multiplicador_2bits_1_s2), .S3(multiplicador_2bits_1_s3));
  multiplicador_2bits multiplicador_2bits_2 (
    .B1(B1), .B0(B0), .A1(A3), .A0(A2), .S0(multiplicador_2bits_2_s0), .S1(multiplicador_2bits_2_s1),
    .S2(multiplicador_2bits_2_s2), .S3(multiplicador_2bits_2_s3));
  multiplicador_2bits multiplicador_2bits_3 (
    .B1(B3), .B0(B2), .A1(A1), .A0(A0), .S0(multiplicador_2bits_3_s0), .S1(multiplicador_2bits_3_s1),
    .S2(multiplicador_2bits_3_s2), .S3(multiplicador_2bits_3_s3));
  multiplicador_2bits multiplicador_2bits_4 (
    .B1(B3), .B0(B2), .A1(A3), .A0(A2), .S0(multiplicador_2bits_4_s0), .S1(multiplicador_2bits_4_s1),
    .S2(multiplicador_2bits_4_s2), .S3(multiplicador_2bits_4_s3));
  soma soma_1 (.A(multiplicador_2bits_1_s3), .B(multiplicador_2bits_2_s2), .Ci(Ci2), .Co(soma_1_co), .S(soma_1_s));
  soma soma_2 (.A(multiplicador_2bits_2_s3), .B(multiplicador_2bits_3_s2), .Ci(Ci3), .Co(soma_2_co), .S(soma_2_s));
  soma soma_3 (.A(multiplicador_2bits_3_s3), .B(multiplicador_2bits_4_s2), .Ci(Ci4), .Co(Ci5), .S(S5));
  meia_soma meia_soma_1 (.A(multiplicador_2bits_4_s3), .B(Ci5), .S(S6), .C(S7));
  meia_soma meia_soma_2 (.A(multiplicador_2bits_1_s1), .B(multiplicador_2bits_2_s0), .S(S1), .C(Ci1));
  soma soma_4 (.A(multiplicador_2bits_1_s2), .B(multiplicador_2bits_2_s1), .Ci(Ci1), .Co(soma_4_co), .S(soma_4_s));
  soma soma_5 (.A(soma_4_s), .B(multiplicador_2bits_3_s0), .Ci(soma_4_co), .Co(Ci2), .S(S2));
  soma soma_6 (.A(soma_1_s), .B(multiplicador_2bits_3_s1), .Ci(soma_1_co), .Co(soma_6_co), .S(soma_6_s));
  soma soma_7 (.A(soma_2_s), .B(multiplicador_2bits_4_s1), .Ci(soma_2_co), .Co(Ci4), .S(S4));
  soma soma_8 (.A(soma_6_s), .B(multiplicador_2bits_4_s0), .Ci(soma_6_co), .Co(Ci3), .S(S3));

  // Other names for the same wires on the sheet: Ci6 = S7
endmodule
