// Digital circuit multiplicador 8bits.dig as structural Verilog
module multiplicador_8bits (
  input  A0,
  input  A1,
  input  A2,
  input  A3,
  input  A4,
  input  A5,
  input  A6,
  input  A7,
  input  B0,
  input  B1,
  input  B2,
  input  B3,
  input  B4,
  input  B5,
  input  B6,
  input  B7,
  output S0,
  output S1,
  output S2,
  output S3,
  output S4,
  output S5,
  output S6,
  output S7,
  output S8,
  output S9,
  output S10,
  output S11,
  output S12,
  output S13,
  output S14,
  output S15
);

  wire and_1_out, and_2_out, and_3_out, and_4_out, and_5_out, and_6_out, and_7_out, and_8_out, and_9_out,
       and_10_out, and_11_out, and_12_out, and_13_out, and_14_out, and_15_out, and_16_out, and_17_out,
       and_18_out, and_19_out, and_20_out, and_21_out, and_22_out, and_23_out, and_24_out, and_25_out,
       and_26_out, and_27_out, and_28_out, and_29_out, and_30_out, and_31_out, and_32_out, and_33_out,
       and_34_out, and_35_out, and_36_out, and_37_out, and_38_out, and_39_out, and_40_out, and_41_out,
       and_42_out, and_43_out, and_44_out, and_45_out, and_46_out, and_47_out, and_48_out, and_49_out,
       and_50_out, and_51_out, and_52_out, and_53_out, and_54_out, and_55_out, and_56_out, and_57_out,
       and_58_out, and_59_out, and_60_out, and_61_out, and_62_out, and_63_out, C1, C2, C3, C4, C5, C6, C7,
       C8, C9, C10, C11, C12, C13, C14, C15, C16, C17, C18, C19, C20, C21, C22, C23, C24, C25, C26, C27, C28,
       C29, C30, C31, C32, C33, C34, C35, C36, C37, C38, C39, C40, C41, C42, C43, C44, C45, C46, C47, C48,
       C49, C50, C51, C52, C53, C54, C55, soma_2_s, soma_4_s, soma_5_s, soma_7_s, soma_8_s, soma_9_s,
       soma_11_s, soma_12_s, soma_13_s, soma_14_s, soma_16_s, soma_17_s, soma_18_s, soma_19_s, soma_20_s,
       soma_22_s, soma_23_s, soma_24_s, soma_25_s, soma_26_s, soma_27_s, soma_28_s, soma_29_s, soma_30_s,
       soma_31_s, soma_32_s, soma_33_s, soma_34_s, soma_35_s, soma_36_s, soma_37_s, soma_38_s, soma_39_s,
       soma_40_s, soma_41_s, soma_42_s, soma_43_s, soma_44_s, soma_45_s, soma_46_s, soma_47_s, soma_48_s;

  and and_1 (and_1_out, B7, A7);
  soma soma_1 (.A(C54), .B(and_1_out), .Ci(C55), .Co(S15), .S(S14));
  and and_2 (and_2_out, B7, A6);
  soma soma_2 (.A(and_3_out), .B(and_2_out), .Ci(C51), .Co(C54), .S(soma_2_s));
  soma soma_3 (.A(C52), .B(soma_2_s), .Ci(C53), .Co(C55), .S(S13));
  and and_3 (and_3_out, B6, A7);
  and and_4 (and_4_out, B6, A6);
  soma soma_4 (.A(and_5_out), .B(and_4_out), .Ci(C47), .Co(C51), .S(soma_4_s));
  soma soma_5 (.A(and_7_out), .B(soma_4_s), .Ci(C48), .Co(C52), .S(soma_5_s));
  soma soma_6 (.A(C49), .B(soma_5_s), .Ci(C50), .Co(C53), .S(S12));
  and and_5 (and_5_out, B5, A7);
  and and_6 (and_6_out, B5, A6);
  and and_7 (and_7_out, B7, A5);
  soma soma_7 (.A(and_8_out), .B(and_6_out), .Ci(C42), .Co(C47), .S(soma_7_s));
  soma soma_8 (.A(and_10_out), .B(soma_7_s), .Ci(C43), .Co(C48), .S(soma_8_s));
  soma soma_9 (.A(and_11_out), .B(soma_8_s), .Ci(C44), .Co(C49), .S(soma_9_s));
  soma soma_10 (.A(C45), .B(soma_9_s), .Ci(C46), .Co(C50), .S(S11));
  and and_8 (and_8_out, B4, A7);
  and and_9 (and_9_out, B4, A6);
  and and_10 (and_10_out, B6, A5);
  and and_11 (and_11_out, B7, A4);
  soma soma_11 (.A(and_12_out), .B(and_9_out), .Ci(C36), .Co(C42), .S(soma_11_s));
  soma soma_12 (.A(and_14_out), .B(soma_11_s), .Ci(C37), .Co(C43), .S(soma_12_s));
  soma soma_13 (.A(and_15_out), .B(soma_12_s), .Ci(C38), .Co(C44), .S(soma_13_s));
  soma soma_14 (.A(and_16_out), .B(soma_13_s), .Ci(C39), .Co(C45), .S(soma_14_s));
  soma soma_15 (.A(C40), .B(soma_14_s), .Ci(C41), .Co(C46), .S(S10));
  and and_12 (and_12_out, B3, A7);
  and and_13 (and_13_out, B3, A6);
  and and_14 (and_14_out, B5, A5);
  and and_15 (and_15_out, B6, A4);
  and and_16 (and_16_out, B7, A3);
  soma soma_16 (.A(and_17_out), .B(and_13_out), .Ci(C29), .Co(C36), .S(soma_16_s));
  soma soma_17 (.A(and_19_out), .B(soma_16_s), .Ci(C30), .Co(C37), .S(soma_17_s));
  soma soma_18 (.A(and_20_out), .B(soma_17_s), .Ci(C31), .Co(C38), .S(soma_18_s));
  soma soma_19 (.A(and_21_out), .B(soma_18_s), .Ci(C32), .Co(C39), .S(soma_19_s));
  soma soma_20 (.A(and_22_out), .B(soma_19_s), .Ci(C33), .Co(C40), .S(soma_20_s));
  soma soma_21 (.A(C34), .B(soma_20_s), .Ci(C35), .Co(C41), .S(S9));
  and and_17 (and_17_out, B2, A7);
  and and_18 (and_18_out, B2, A6);
  and and_19 (and_19_out, B4, A5);
  and and_20 (and_20_out, B5, A4);
  and and_21 (and_21_out, B6, A3);
  and and_22 (and_22_out, B7, A2);
  soma soma_22 (.A(and_23_out), .B(and_18_out), .Ci(C22), .Co(C29), .S(soma_22_s));
  soma soma_23 (.A(and_25_out), .B(soma_22_s), .Ci(C23), .Co(C30), .S(soma_23_s));
  soma soma_24 (.A(and_26_out), .B(soma_23_s), .Ci(C24), .Co(C31), .S(soma_24_s));
  soma soma_25 (.A(and_27_out), .B(soma_24_s), .Ci(C25), .Co(C32), .S(soma_25_s));
  soma soma_26 (.A(and_28_out), .B(soma_25_s), .Ci(C26), .Co(C33), .S(soma_26_s));
  soma soma_27 (.A(and_29_out), .B(soma_26_s), .Ci(C27), .Co(C34), .S(soma_27_s));
  meia_soma meia_soma_1 (.A(soma_27_s), .B(C28), .S(S8), .C(C35));
  and and_23 (and_23_out, B1, A7);
  and and_24 (and_24_out, B1, A6);
  and and_25 (and_25_out, B3, A5);
  and and_26 (and_26_out, B4, A4);
  and and_27 (and_27_out, B5, A3);
  and and_28 (and_28_out, B6, A2);
  and and_29 (and_29_out, B7, A1);
  soma soma_28 (.A(and_30_out), .B(and_24_out), .Ci(C16), .Co(C22), .S(soma_28_s));
  soma soma_29 (.A(and_32_out), .B(soma_28_s), .Ci(C17), .Co(C23), .S(soma_29_s));
  soma soma_30 (.A(and_33_out), .B(soma_29_s), .Ci(C18), .Co(C24), .S(soma_30_s));
  soma soma_31 (.A(and_34_out), .B(soma_30_s), .Ci(C19), .Co(C25), .S(soma_31_s));
  soma soma_32 (.A(and_35_out), .B(soma_31_s), .Ci(C20), .Co(C26), .S(soma_32_s));
  soma soma_33 (.A(and_36_out), .B(soma_32_s), .Ci(C21), .Co(C27), .S(soma_33_s));
  meia_soma meia_soma_2 (.A(and_37_out), .B(soma_33_s), .S(S7), .C(C28));
  and and_30 (and_30_out, B0, A7);
  and and_31 (and_31_out, B1, A5);
  and and_32 (and_32_out, B2, A5);
  and and_33 (and_33_out, B3, A4);
  and and_34 (and_34_out, B4, A3);
  and and_35 (and_35_out, B5, A2);
  and and_36 (and_36_out, B6, A1);
  and and_37 (and_37_out, B7, A0);
  soma soma_34 (.A(and_38_out), .B(and_31_out), .Ci(C11), .Co(C16), .S(soma_34_s));
  soma soma_35 (.A(and_40_out), .B(soma_34_s), .Ci(C12), .Co(C17), .S(soma_35_s));
  soma soma_36 (.A(and_41_out), .B(soma_35_s), .Ci(C13), .Co(C18), .S(soma_36_s));
  soma soma_37 (.A(and_42_out), .B(soma_36_s), .Ci(C14), .Co(C19), .S(soma_37_s));
  soma soma_38 (.A(and_43_out), .B(soma_37_s), .Ci(C15), .Co(C20), .S(soma_38_s));
  meia_soma meia_soma_3 (.A(and_44_out), .B(soma_38_s), .S(S6), .C(C21));
  and and_38 (and_38_out, B0, A6);
  and and_39 (and_39_out, B1, A4);
  and and_40 (and_40_out, B2, A4);
  and and_41 (and_41_out, B3, A3);
  and and_42 (and_42_out, B4, A2);
  and and_43 (and_43_out, B5, A1);
  and and_44 (and_44_out, B6, A0);
  soma soma_39 (.A(and_45_out), .B(and_39_out), .Ci(C7), .Co(C11), .S(soma_39_s));
  soma soma_40 (.A(and_47_out), .B(soma_39_s), .Ci(C8), .Co(C12), .S(soma_40_s));
  soma soma_41 (.A(and_48_out), .B(soma_40_s), .Ci(C9), .Co(C13), .S(soma_41_s));
  soma soma_42 (.A(and_49_out), .B(soma_41_s), .Ci(C10), .Co(C14), .S(soma_42_s));
  meia_soma meia_soma_4 (.A(and_50_out), .B(soma_42_s), .S(S5), .C(C15));
  and and_45 (and_45_out, B0, A5);
  and and_46 (and_46_out, B1, A3);
  and and_47 (and_47_out, B2, A3);
  and and_48 (and_48_out, B3, A2);
  and and_49 (and_49_out, B4, A1);
  and and_50 (and_50_out, B5, A0);
  soma soma_43 (.A(and_51_out), .B(and_46_out), .Ci(C4), .Co(C7), .S(soma_43_s));
  soma soma_44 (.A(and_53_out), .B(soma_43_s), .Ci(C5), .Co(C8), .S(soma_44_s));
  soma soma_45 (.A(and_54_out), .B(soma_44_s), .Ci(C6), .Co(C9), .S(soma_45_s));
  meia_soma meia_soma_5 (.A(and_55_out), .B(soma_45_s), .S(S4), .C(C10));
  and and_51 (and_51_out, B0, A4);
  and and_52 (and_52_out, B1, A2);
  and and_53 (and_53_out, B2, A2);
  and and_54 (and_54_out, B3, A1);
  and and_55 (and_55_out, B4, A0);
  soma soma_46 (.A(and_56_out), .B(and_52_out), .Ci(C2), .Co(C4), .S(soma_46_s));
  soma soma_47 (.A(and_58_out), .B(soma_46_s), .Ci(C3), .Co(C5), .S(soma_47_s));
  meia_soma meia_soma_6 (.A(and_59_out), .B(soma_47_s), .S(S3), .C(C6));
  and and_56 (and_56_out, B0, A3);
  and and_57 (and_57_out, B1, A1);
  and and_58 (and_58_out, B2, A1);
  and and_59 (and_59_out, B3, A0);
  soma soma_48 (.A(and_60_out), .B(and_57_out), .Ci(C1), .Co(C2), .S(soma_48_s));
  meia_soma meia_soma_7 (.A(and_62_out), .B(soma_48_s), .S(S2), .C(C3));
  and and_60 (and_60_out, B0, A2);
  and and_61 (and_61_out, B1, A0);
  and and_62 (and_62_out, B2, A0);
  meia_soma meia_soma_8 (.A(and_63_out), .B(and_61_out), .S(S1), .C(C1));
  and and_63 (and_63_out, B0, A1);
  and and_64 (S0, B0, A0);
endmodule
