// Digital circuit multiplicador.dig as structural Verilog
module multiplicador (
  input  B1,
  input  B0,
  input  A1,
  input  A0,
  output S3,
  output S2,
  output S1,
  output S0
);

  wire and_2_out, and_3_out, and_4_out, and_5_out, and_6_out, and_7_out, not_1_out, not_2_out, not_3_out,
       not_4_out;

  not not_1 (not_1_out, B1);
  not not_2 (not_2_out, B0);
  not not_3 (not_3_out, A1);
  not not_4 (not_4_out, A0);
  and and_1 (S3, B0, B1, A0, A1);
  and and_2 (and_2_out, not_2_out, B1, A1);
  and and_3 (and_3_out, B1, not_4_out, A1);
  and and_4 (and_4_out, B0, not_1_out, A1);
  and and_5 (and_5_out, not_2_out, B1, A0);
  and and_6 (and_6_out, B0, not_4_out, A1);
  and and_7 (and_7_out, B1, A0, not_3_out);
  and and_8 (S0, B0, A0);
  or or_1 (S2, and_2_out, and_3_out);
  or or_2 (S1, and_4_out, and_5_out, and_6_out, and_7_out);
endmodule
