// Digital circuit shift lógico.dig as structural Verilog
module \shift_lógico  (
  input  B0,
  input  B1,
  input  B2,
  input  B3,
  input  B4,
  input  B5,
  input  B6,
  input  B7,
  input  Dir,
  output S0,
  output S1,
  output S2,
  output S3,
  output S4,
  output S5,
  output S6,
  output S7
);

  Multiplexer multiplexer_1 (.sel(Dir), .in_0(1'b0), .in_1(B1), .out(S0));
  Multiplexer multiplexer_2 (.sel(Dir), .in_0(B0), .in_1(B2), .out(S1));
  Multiplexer multiplexer_3 (.sel(Dir), .in_0(B1), .in_1(B3), .out(S2));
  Multiplexer multiplexer_4 (.sel(Dir), .in_0(B2), .in_1(B4), .out(S3));
  Multiplexer multiplexer_5 (.sel(Dir), .in_0(B3), .in_1(B5), .out(S4));
  Multiplexer multiplexer_6 (.sel(Dir), .in_0(B4), .in_1(B6), .out(S5));
  Multiplexer multiplexer_7 (.sel(Dir), .in_0(B5), .in_1(B7), .out(S6));
  Multiplexer multiplexer_8 (.sel(Dir), .in_0(B6), .in_1(1'b0), .out(S7));
endmodule
