// Digital circuit somador 4bits.dig as structural Verilog
module somador_4bits (
  input  B0,
  input  A0,
  input  Ci,
  input  B1,
  input  A1,
  input  B2,
  input  A2,
  input  B3,
  input  A3,
  output S0,
  output S1,
  output S2,
  output S3,
  output Co
);

  wire soma_2_co, soma_3_co, soma_4_co;

  soma soma_1 (.A(A3), .B(B3), .Ci(soma_2_co), .Co(Co), .S(S3));
  soma soma_2 (.A(A2), .B(B2), .Ci(soma_3_co), .Co(soma_2_co), .S(S2));
  soma soma_3 (.A(A1), .B(B1), .Ci(soma_4_co), .Co(soma_3_co), .S(S1));
  soma soma_4 (.A(A0), .B(B0), .Ci(Ci), .Co(soma_4_co), .S(S0));
endmodule
