// Digital circuit somador 8bits.dig as structural Verilog
module somador_8bits (
  input  A0,
  input  B0,
  input  A1,
  input  B1,
  input  A2,
  input  B2,
  input  A3,
  input  B3,
  input  A4,
  input  B4,
  input  A5,
  input  B5,
  input  A6,
  input  B6,
  input  A7,
  input  B7,
  input  Ci,
  output S0,
  output S1,
  output S2,
  output S3,
  output S4,
  output S5,
  output S6,
  output S7,
  output Co
);

  wire Co_t;

  somador_4bits somador_4bits_1 (
    .B0(B0), .A0(A0), .Ci(Ci), .B1(B1), .A1(A1), .B2(B2), .A2(A2), .B3(B3), .A3(A3), .S0(S0), .S1(S1),
    .S2(S2), .S3(S3), .Co(Co_t));
  somador_4bits somador_4bits_2 (
    .B0(B4), .A0(A4), .Ci(Co_t), .B1(B5), .A1(A5), .B2(B6), .A2(A6), .B3(B7), .A3(A7), .S0(S4), .S1(S5),
    .S2(S6), .S3(S7), .Co(Co));
endmodule
