// Digital circuit somador-subtrador-aula.dig as structural Verilog
module somador_subtrador_aula (
  input  [7:0] A,
  input  [7:0] B,
  input  Sel
);

  wire button_1_out;
  wire [7:0] add_1_s, d_ff_1_q, multiplexer_1_out, sub_1_s;

  Add #(.Bits(8)) add_1 (.a(A), .b(B), .c_i(1'b0), .s(add_1_s));  // open: c_o
  Sub #(.Bits(8)) sub_1 (.a(A), .b(B), .c_i(1'b0), .s(sub_1_s));  // open: c_o
  Multiplexer #(.Bits(8)) multiplexer_1 (.sel(Sel), .in_0(add_1_s), .in_1(sub_1_s), .out(multiplexer_1_out));
  D_FF #(.Bits(8)) d_ff_1 (.D(multiplexer_1_out), .C(button_1_out), .Q(d_ff_1_q));  // open: nQ
  Button button_1 (.out(button_1_out));
  Seven_Seg_Hex seven_seg_hex_1 (.d(d_ff_1_q[7:4]), .dp(1'b0));
  Seven_Seg_Hex seven_seg_hex_2 (.d(d_ff_1_q[3:0]), .dp(1'b0));
endmodule
