// Digital circuit subtrator 4bits.dig as structural Verilog
module subtrator_4bits (
  input  A0,
  input  B0,
  input  A1,
  input  B1,
  input  A2,
  input  B2,
  input  A3,
  input  B3,
  input  Ci,
  output S0,
  output S1,
  output S2,
  output S3,
  output Co
);

  wire subtrator_1_co, subtrator_2_co, subtrator_3_co;

  subtrator subtrator_1 (.A(A0), .B(B0), .Ci(Ci), .Co(subtrator_1_co), .S(S0));
  subtrator subtrator_2 (.A(A1), .B(B1), .Ci(subtrator_1_co), .Co(subtrator_2_co), .S(S1));
  subtrator subtrator_3 (.A(A2), .B(B2), .Ci(subtrator_2_co), .Co(subtrator_3_co), .S(S2));
  subtrator subtrator_4 (.A(A3), .B(B3), .Ci(subtrator_3_co), .Co(Co), .S(S3));
endmodule
