// Digital circuit subtrator.dig as structural Verilog
module subtrator (
  input  A,
  input  B,
  input  Ci,
  output Co,
  output S
);

  wire meio_subtrator_1_co, meio_subtrator_1_s, meio_subtrator_2_co;

  meio_subtrator meio_subtrator_1 (.A(A), .B(B), .S(meio_subtrator_1_s), .Co(meio_subtrator_1_co));
  meio_subtrator meio_subtrator_2 (.A(meio_subtrator_1_s), .B(Ci), .S(S), .Co(meio_subtrator_2_co));
  or or_1 (Co, meio_subtrator_2_co, meio_subtrator_1_co);
endmodule
